# Fritzing sketch TinyDuino 2114 RAM (saved by Fritzing 0.9.9b)
breadboards: 1

parts:
  74LS1 = DIP - 20 pins [package="DIP (Dual Inline) [THT]"]
  74LS2 = DIP - 20 pins [package="DIP (Dual Inline) [THT]"]
  74LS3 = DIP - 14 pins [package="DIP (Dual Inline) [THT]"]
  C1 = Ceramic Capacitor [capacitance=100nF voltage=35V package="100 mil [THT, multilayer]"]
  C2 = Ceramic Capacitor [capacitance=100nF voltage=35V package="100 mil [THT, multilayer]"]
  C3 = Ceramic Capacitor [capacitance=100nF voltage=35V package="100 mil [THT, multilayer]"]
  C4 = Electrolytic Capacitor [capacitance=10µF voltage=35V package="100 mil [THT, electrolytic]"]
  S1 = Pushbutton [package="[THT]"]  # not connected
  C5 = Ceramic Capacitor [capacitance=100nF voltage=35V package="100 mil [THT, multilayer]"]
  2114A-1 = P2114A-4 - 18 pins [package="DIP (Dual Inline) [THT]"]
  J1 = Connector - 8 pins [package=THT]

nets:
  N1: 74LS1.S0, 74LS1.~CLR, 74LS2.S0, 74LS2.~CLR, 74LS3.D0_A, 74LS3.D1_B, 74LS3.D2_C, 74LS3.D3_D
  N2: 74LS1.~OE1, 74LS1.~OE2, 74LS1.S1, J1.7_A5:LDE
  N3: 74LS1.D6_QG, 2114A-1.D1
  N4: 74LS1.D4_QE, 2114A-1.D3
  GND: 74LS1.GND, 74LS2.GND, 74LS3.MODE, 74LS3.GND, C1.0, C2.0, C3.0, C5.0, 2114A-1.GND, J1.0:_GND
  N5: 74LS1.SR_Ds0, 74LS2.QH'_Q7
  N6: 74LS1.CLK, J1.6_A4:CLKD
  N7: 74LS1.QF_D5, 2114A-1.D2
  N8: 74LS1.QH_D7, 2114A-1.D0
  N9: 74LS1.QH'_Q7, J1.2:_A0:Dsi
  VCC: 74LS1.SL_Ds7, 74LS1.Vcc, 74LS2.SL_Ds7, 74LS2.Vcc, 74LS3.Vcc, C1.1, C2.1, C3.1, C4.+, C5.1, 2114A-1.Vcc
  N10: 74LS2.~OE1, 74LS2.~OE2, 74LS2.S1, 74LS3.CLK_2, C4.-
  N11: 74LS2.D6_QG, 2114A-1.A1
  N12: 74LS2.D4_QE, 2114A-1.A3
  N13: 74LS2.D2_QC, 2114A-1.A5
  N14: 74LS2.D0_QA, 2114A-1.A7
  N15: 74LS2.SR_Ds0, 74LS3.QD_Q3, 2114A-1.A8
  N16: 74LS2.CLK, 74LS3.CLK_1, J1.3_A1:CLKA
  N17: 74LS2.QB_D1, 2114A-1.A6
  N18: 74LS2.QD_D3, 2114A-1.A4
  N19: 74LS2.QF_D5, 2114A-1.A2
  N20: 74LS2.QH_D7, 2114A-1.A0
  N21: 74LS3.Ds_SER, J1.1:_P4:Dso
  N22: 74LS3.QC_Q2, 2114A-1.A9
  N23: 2114A-1.~CS, J1.4_A2:~CS
  N24: 2114A-1.R/~W, J1.5_A3:R/~W

notes:
  U2
  1   2   3   4   5   6   7   8
  2114 RAM Test
  TinyDuino Pin4
  U4
  U3
  1   3   5   7
  0   2   4   6
  U1
  6   5   4   3   0   1   2  CS
  7   8   9   0   1   2   3  RW
  11  10  8   9

custom parts:
  DIP - 20 pins: 8-Bit Universal Shift/Storage Register
  DIP - 14 pins: 4-Bit Parallel Access Shift Register
  P2114A-4 - 18 pins: Intel P2114A-4 1Kx4 Static RAM. With 18 pins on a 300mil dual inline package (DIP) footprint.
  Connector - 8 pins: Connector with 8 pins on a 100 mil inline pin header footprint.
