# Fritzing sketch TinyDuino Mk2716 Reader - Shift Register Test (saved by Fritzing 0.9.9b)
breadboards: 8

parts:
  74LS1 = DIP - 20 pins [package="DIP (Dual Inline) [THT]"]
  74LS2 = DIP - 20 pins [package="DIP (Dual Inline) [THT]"]
  74LS3 = DIP - 14 pins [package="DIP (Dual Inline) [THT]"]
  C1 = Ceramic Capacitor [capacitance=100nF voltage=35V package="100 mil [THT, multilayer]"]
  C2 = Ceramic Capacitor [capacitance=100nF voltage=35V package="100 mil [THT, multilayer]"]
  C3 = Ceramic Capacitor [capacitance=100nF voltage=35V package="100 mil [THT, multilayer]"]
  U1 = mystery part, 6 pins [chip_label="TinyDuino Conn"]
  C4 = Electrolytic Capacitor [capacitance=10µF voltage=35V package="100 mil [THT, electrolytic]"]  # not connected
  74LS4 = DIP - 20 pins [package="DIP (Dual Inline) [THT]"]
  74LS5 = DIP - 20 pins [package="DIP (Dual Inline) [THT]"]
  74LS6 = DIP - 14 pins [package="DIP (Dual Inline) [THT]"]
  C5 = Ceramic Capacitor [capacitance=100nF voltage=35V package="100 mil [THT, multilayer]"]
  C6 = Ceramic Capacitor [capacitance=100nF voltage=35V package="100 mil [THT, multilayer]"]
  U2 = mystery part, 6 pins [chip_label="TinyDuino Conn"]
  C7 = Ceramic Capacitor [capacitance=100nF voltage=35V package="100 mil [THT, multilayer]"]
  C8 = Electrolytic Capacitor [capacitance=10µF voltage=35V package="100 mil [THT, electrolytic]"]  # not connected
  74LS7 = DIP - 20 pins [package="DIP (Dual Inline) [THT]"]
  74LS8 = DIP - 20 pins [package="DIP (Dual Inline) [THT]"]
  74LS9 = DIP - 14 pins [package="DIP (Dual Inline) [THT]"]
  C9 = Ceramic Capacitor [capacitance=100nF voltage=35V package="100 mil [THT, multilayer]"]
  C10 = Ceramic Capacitor [capacitance=100nF voltage=35V package="100 mil [THT, multilayer]"]
  U3 = mystery part, 6 pins [chip_label="TinyDuino Conn"]
  C11 = Ceramic Capacitor [capacitance=100nF voltage=35V package="100 mil [THT, multilayer]"]
  C12 = Electrolytic Capacitor [capacitance=10µF voltage=35V package="100 mil [THT, electrolytic]"]  # not connected
  74LS10 = DIP - 20 pins [package="DIP (Dual Inline) [THT]"]
  74LS11 = DIP - 20 pins [package="DIP (Dual Inline) [THT]"]
  74LS12 = DIP - 14 pins [package="DIP (Dual Inline) [THT]"]
  C13 = Ceramic Capacitor [capacitance=100nF voltage=35V package="100 mil [THT, multilayer]"]
  C14 = Ceramic Capacitor [capacitance=100nF voltage=35V package="100 mil [THT, multilayer]"]
  U4 = mystery part, 6 pins [chip_label="TinyDuino Conn"]
  C15 = Ceramic Capacitor [capacitance=100nF voltage=35V package="100 mil [THT, multilayer]"]
  C16 = Electrolytic Capacitor [capacitance=10µF voltage=35V package="100 mil [THT, electrolytic]"]  # not connected
  S1 = Pushbutton [package="[THT]"]  # not connected

nets:
  N1: 74LS1.S0, 74LS1.~CLR, 74LS2.S0, 74LS2.~CLR, 74LS3.D0_A, 74LS3.D1_B, 74LS3.D2_C, 74LS3.D3_D
  N2: 74LS1.~OE1, 74LS1.~OE2, 74LS1.S1, U1.pin6
  N3: 74LS1.D6_QG, 74LS2.D6_QG
  N4: 74LS1.D4_QE, 74LS2.D4_QE
  N5: 74LS1.D2_QC, 74LS2.D2_QC
  N6: 74LS1.D0_QA, 74LS2.D0_QA
  GND: 74LS1.GND, 74LS2.~OE1, 74LS2.~OE2, 74LS2.GND, 74LS2.S1, 74LS3.MODE, 74LS3.GND, C1.0, C2.0, C3.0
  VCC: 74LS1.SR_Ds0, 74LS1.SL_Ds7, 74LS1.Vcc, 74LS2.SL_Ds7, 74LS2.Vcc, 74LS3.Vcc, C1.1, C2.1, C3.1
  N7: 74LS1.CLK, U1.pin5
  N8: 74LS1.QB_D1, 74LS2.QB_D1
  N9: 74LS1.QD_D3, 74LS2.QD_D3
  N10: 74LS1.QF_D5, 74LS2.QF_D5
  N11: 74LS1.QH_D7, 74LS2.QH_D7
  N12: 74LS1.QH'_Q7, U1.pin1
  N13: 74LS2.SR_Ds0, 74LS3.QD_Q3
  N14: 74LS2.CLK, 74LS3.CLK_1, U1.pin2
  N15: 74LS4.S0, 74LS4.~CLR, 74LS5.S0, 74LS5.~CLR, 74LS6.D0_A, 74LS6.D1_B, 74LS6.D2_C, 74LS6.D3_D
  N16: 74LS4.~OE1, 74LS4.~OE2, 74LS4.S1, U2.pin6
  N17: 74LS4.D6_QG, 74LS5.D6_QG
  N18: 74LS4.D4_QE, 74LS5.D4_QE
  N19: 74LS4.D2_QC, 74LS5.D2_QC
  N20: 74LS4.D0_QA, 74LS5.D0_QA
  GND_2: 74LS4.GND, 74LS5.~OE1, 74LS5.~OE2, 74LS5.GND, 74LS5.S1, 74LS6.MODE, 74LS6.GND, C5.0, C6.0, C7.0
  VCC_2: 74LS4.SR_Ds0, 74LS4.SL_Ds7, 74LS4.Vcc, 74LS5.SL_Ds7, 74LS5.Vcc, 74LS6.Vcc, C5.1, C6.1, C7.1
  N21: 74LS4.CLK, U2.pin5
  N22: 74LS4.QB_D1, 74LS5.QB_D1
  N23: 74LS4.QD_D3, 74LS5.QD_D3
  N24: 74LS4.QF_D5, 74LS5.QF_D5
  N25: 74LS4.QH_D7, 74LS5.QH_D7
  N26: 74LS5.SR_Ds0, 74LS6.QD_Q3, U2.pin1
  N27: 74LS5.CLK, 74LS6.CLK_1, U2.pin2
  N28: 74LS7.S0, 74LS7.~CLR, 74LS8.S0, 74LS8.~CLR, 74LS9.D0_A, 74LS9.D1_B, 74LS9.D2_C, 74LS9.D3_D
  N29: 74LS7.~OE1, 74LS7.~OE2, 74LS7.S1, U3.pin6
  N30: 74LS7.D6_QG, 74LS8.D6_QG
  N31: 74LS7.D4_QE, 74LS8.D4_QE
  N32: 74LS7.D2_QC, 74LS8.D2_QC
  N33: 74LS7.D0_QA, 74LS8.D0_QA
  GND_3: 74LS7.GND, 74LS8.~OE1, 74LS8.~OE2, 74LS8.GND, 74LS8.S1, 74LS9.MODE, 74LS9.GND, C9.0, C10.0, C11.0
  N34: 74LS7.CLK, U3.pin5
  N35: 74LS7.QB_D1, 74LS8.QB_D1
  N36: 74LS7.QD_D3, 74LS8.QD_D3
  N37: 74LS7.QF_D5, 74LS8.QF_D5
  N38: 74LS7.QH_D7, 74LS8.QH_D7
  N39: 74LS7.QH'_Q7, U3.pin1
  VCC_3: 74LS7.SL_Ds7, 74LS7.Vcc, 74LS8.SL_Ds7, 74LS8.Vcc, 74LS9.Vcc, C9.1, C10.1, C11.1
  N40: 74LS8.SR_Ds0, 74LS9.QD_Q3
  N41: 74LS8.CLK, 74LS9.CLK_1, U3.pin2
  N42: 74LS10.S0, 74LS10.~CLR, 74LS11.S0, 74LS11.~CLR, 74LS12.D0_A, 74LS12.D1_B, 74LS12.D2_C, 74LS12.D3_D
  N43: 74LS10.~OE1, 74LS10.~OE2, 74LS10.S1, U4.pin6
  N44: 74LS10.D6_QG, 74LS11.D6_QG
  N45: 74LS10.D4_QE, 74LS11.D4_QE
  N46: 74LS10.D2_QC, 74LS11.D2_QC
  N47: 74LS10.D0_QA, 74LS11.D0_QA
  GND_4: 74LS10.GND, 74LS11.~OE1, 74LS11.~OE2, 74LS11.GND, 74LS11.S1, 74LS12.MODE, 74LS12.GND, C14.0, C15.0
  VCC_4: 74LS10.SR_Ds0, 74LS10.SL_Ds7, 74LS10.Vcc, 74LS11.SL_Ds7, 74LS11.Vcc, 74LS12.Vcc, C13.1, C14.1, C15.1
  N48: 74LS10.CLK, U4.pin5
  N49: 74LS10.QB_D1, 74LS11.QB_D1
  N50: 74LS10.QD_D3, 74LS11.QD_D3
  N51: 74LS10.QF_D5, 74LS11.QF_D5
  N52: 74LS10.QH_D7, 74LS11.QH_D7
  N53: 74LS11.SR_Ds0, 74LS12.QD_Q3
  N54: 74LS11.CLK, 74LS12.CLK_1, U4.pin2
  N55: 74LS11.QH'_Q7, U4.pin1

notes:
  U4
  U3
  U2
  1 2 3 4 5 6
  Mk2716 Reader - Shift Register Test - Address Register >> Data Register Loop
  Mk2716 Reader - Shift Register Test - Address High
  Mk2716 Reader - Shift Register Test - Data Register
  TinyDuino Pin4
  Mk2716 Reader - Shift Register Test - Address Register

custom parts:
  DIP - 20 pins: 8-Bit Universal Shift/Storage Register
  DIP - 14 pins: 4-Bit Parallel Access Shift Register
