# Fritzing sketch TinyDuino Mk2716 Reader + Unit Tests (saved by Fritzing 0.9.9b)
breadboards: 5

parts:
  74LS1 = DIP - 20 pins [package="DIP (Dual Inline) [THT]"]
  74LS2 = DIP - 20 pins [package="DIP (Dual Inline) [THT]"]
  74LS3 = DIP - 14 pins [package="DIP (Dual Inline) [THT]"]
  C1 = Ceramic Capacitor [capacitance=100nF voltage=35V package="100 mil [THT, multilayer]"]
  C2 = Ceramic Capacitor [capacitance=100nF voltage=35V package="100 mil [THT, multilayer]"]
  C3 = Ceramic Capacitor [capacitance=100nF voltage=35V package="100 mil [THT, multilayer]"]
  C4 = Electrolytic Capacitor [capacitance=10µF voltage=35V package="100 mil [THT, electrolytic]"]
  S1 = Pushbutton [package="[THT]"]  # not connected
  C5 = Ceramic Capacitor [capacitance=100nF voltage=35V package="100 mil [THT, multilayer]"]
  MK2716T1 = DIP - 24 pins [package="DIP (Dual Inline) [THT]"]
  U1 = mystery part, 8 pins [chip_label="TinyDuino Conn"]
  C6 = Ceramic Capacitor [capacitance=100nF voltage=35V package="100 mil [THT, multilayer]"]
  74LS4 = DIP - 14 pins [package="DIP (Dual Inline) [THT]"]
  U2 = mystery part, 8 pins [chip_label="TinyDuino Conn"]
  74LS5 = DIP - 20 pins [package="DIP (Dual Inline) [THT]"]
  C7 = Ceramic Capacitor [capacitance=100nF voltage=35V package="100 mil [THT, multilayer]"]
  74LS6 = DIP - 20 pins [package="DIP (Dual Inline) [THT]"]
  C8 = Ceramic Capacitor [capacitance=100nF voltage=35V package="100 mil [THT, multilayer]"]
  C9 = Electrolytic Capacitor [capacitance=10µF voltage=35V package="100 mil [THT, electrolytic]"]
  C10 = Ceramic Capacitor [capacitance=100nF voltage=35V package="100 mil [THT, multilayer]"]
  IC1 = IC, DIP package, 24 pins [chip_label=JAD]
  C11 = Ceramic Capacitor [capacitance=100nF voltage=35V package="100 mil [THT, multilayer]"]
  74LS7 = DIP - 14 pins [package="DIP (Dual Inline) [THT]"]
  U3 = mystery part, 8 pins [chip_label="TinyDuino Conn"]
  74LS8 = DIP - 20 pins [package="DIP (Dual Inline) [THT]"]
  C12 = Ceramic Capacitor [capacitance=100nF voltage=35V package="100 mil [THT, multilayer]"]
  74LS9 = DIP - 20 pins [package="DIP (Dual Inline) [THT]"]
  C13 = Ceramic Capacitor [capacitance=100nF voltage=35V package="100 mil [THT, multilayer]"]
  C14 = Electrolytic Capacitor [capacitance=10µF voltage=35V package="100 mil [THT, electrolytic]"]
  C15 = Ceramic Capacitor [capacitance=100nF voltage=35V package="100 mil [THT, multilayer]"]
  IC2 = IC, DIP package, 24 pins [chip_label=JAD]
  C16 = Ceramic Capacitor [capacitance=100nF voltage=35V package="100 mil [THT, multilayer]"]
  74LS10 = DIP - 14 pins [package="DIP (Dual Inline) [THT]"]
  U4 = mystery part, 8 pins [chip_label="TinyDuino Conn"]
  74LS11 = DIP - 20 pins [package="DIP (Dual Inline) [THT]"]
  C17 = Ceramic Capacitor [capacitance=100nF voltage=35V package="100 mil [THT, multilayer]"]
  74LS12 = DIP - 20 pins [package="DIP (Dual Inline) [THT]"]
  C18 = Ceramic Capacitor [capacitance=100nF voltage=35V package="100 mil [THT, multilayer]"]
  C19 = Electrolytic Capacitor [capacitance=10µF voltage=35V package="100 mil [THT, electrolytic]"]
  C20 = Ceramic Capacitor [capacitance=100nF voltage=35V package="100 mil [THT, multilayer]"]
  IC3 = IC, DIP package, 24 pins [chip_label=JAD]
  C21 = Ceramic Capacitor [capacitance=100nF voltage=35V package="100 mil [THT, multilayer]"]
  74LS13 = DIP - 14 pins [package="DIP (Dual Inline) [THT]"]
  U5 = mystery part, 8 pins [chip_label="TinyDuino Conn"]
  74LS14 = DIP - 20 pins [package="DIP (Dual Inline) [THT]"]
  C22 = Ceramic Capacitor [capacitance=100nF voltage=35V package="100 mil [THT, multilayer]"]
  74LS15 = DIP - 20 pins [package="DIP (Dual Inline) [THT]"]
  C23 = Ceramic Capacitor [capacitance=100nF voltage=35V package="100 mil [THT, multilayer]"]
  C24 = Electrolytic Capacitor [capacitance=10µF voltage=35V package="100 mil [THT, electrolytic]"]
  C25 = Ceramic Capacitor [capacitance=100nF voltage=35V package="100 mil [THT, multilayer]"]
  IC4 = IC, DIP package, 24 pins [chip_label=JAD]

nets:
  N1: 74LS1.S0, 74LS1.~CLR, 74LS2.S0, 74LS2.~CLR, 74LS3.D0_A, 74LS3.D1_B, 74LS3.D2_C, 74LS3.D3_D
  N2: 74LS1.~OE1, 74LS1.~OE2, 74LS1.S1, U1.pin1
  N3: 74LS1.D6_QG, MK2716T1.D1
  N4: 74LS1.D4_QE, MK2716T1.D3
  N5: 74LS1.D2_QC, MK2716T1.D5
  N6: 74LS1.D0_QA, MK2716T1.D7
  GND: 74LS1.GND, 74LS2.GND, 74LS3.MODE, 74LS3.GND, C1.0, C2.0, C3.0, C5.0, MK2716T1.GND, U1.pin8
  VCC: 74LS1.SR_Ds0, 74LS1.SL_Ds7, 74LS1.Vcc, 74LS2.SL_Ds7, 74LS2.Vcc, 74LS3.Vcc, C1.1, C2.1, C3.1, C4.+, C5.1, MK2716T1.Vpp, MK2716T1.VCC
  N7: 74LS1.CLK, U1.pin2
  N8: 74LS1.QB_D1, MK2716T1.D6
  N9: 74LS1.QD_D3, MK2716T1.D4
  N10: 74LS1.QF_D5, MK2716T1.D2
  N11: 74LS1.QH_D7, MK2716T1.D0
  N12: 74LS1.QH'_Q7, U1.pin6
  N13: 74LS2.~OE1, 74LS2.~OE2, 74LS2.S1, 74LS3.CLK_2, C4.-
  N14: 74LS2.D6_QG, MK2716T1.A1
  N15: 74LS2.D4_QE, MK2716T1.A3
  N16: 74LS2.D2_QC, MK2716T1.A5
  N17: 74LS2.D0_QA, MK2716T1.A7
  N18: 74LS2.SR_Ds0, 74LS3.QD_Q3, MK2716T1.A8
  N19: 74LS2.CLK, 74LS3.CLK_1, U1.pin5
  N20: 74LS2.QB_D1, MK2716T1.A6
  N21: 74LS2.QD_D3, MK2716T1.A4
  N22: 74LS2.QF_D5, MK2716T1.A2
  N23: 74LS2.QH_D7, MK2716T1.A0
  N24: 74LS3.Ds_SER, U1.pin7
  N25: 74LS3.QC_Q2, MK2716T1.A9
  N26: 74LS3.QB_Q1, MK2716T1.A10
  N27: MK2716T1.~CE, U1.pin4
  N28: MK2716T1.~OE, U1.pin3
  GND_2: C6.0, 74LS4.MODE, 74LS4.GND, U2.pin8, 74LS5.GND, C7.0, 74LS6.GND, C8.0, C10.0, IC1.pin12
  VCC_2: C6.1, 74LS4.Vcc, 74LS5.SR_Ds0, 74LS5.SL_Ds7, 74LS5.Vcc, C7.1, 74LS6.SL_Ds7, 74LS6.Vcc, C8.1, C9.+, C10.1, IC1.pin21, IC1.pin24
  N29: 74LS4.Ds_SER, U2.pin7
  N30: 74LS4.D0_A, 74LS4.D1_B, 74LS4.D2_C, 74LS4.D3_D, 74LS5.S0, 74LS5.~CLR, 74LS6.S0, 74LS6.~CLR
  N31: 74LS4.CLK_2, 74LS6.~OE1, 74LS6.~OE2, 74LS6.S1, C9.-
  N32: 74LS4.CLK_1, U2.pin5, 74LS6.CLK
  N33: 74LS4.QD_Q3, 74LS6.SR_Ds0, IC1.pin23
  N34: 74LS4.QC_Q2, IC1.pin22
  N35: 74LS4.QB_Q1, IC1.pin19
  N36: U2.pin1, 74LS5.~OE1, 74LS5.~OE2, 74LS5.S1
  N37: U2.pin2, 74LS5.CLK
  N38: U2.pin3, IC1.pin20
  N39: U2.pin4, IC1.pin18
  N40: U2.pin6, 74LS5.QH'_Q7
  N41: 74LS5.D6_QG, 74LS6.D6_QG, IC1.pin7, IC1.pin10
  N42: 74LS5.D4_QE, 74LS6.D4_QE, IC1.pin5, IC1.pin13
  N43: 74LS5.D2_QC, 74LS6.D2_QC, IC1.pin3, IC1.pin15
  N44: 74LS5.D0_QA, 74LS6.D0_QA, IC1.pin1, IC1.pin17
  N45: 74LS5.QB_D1, 74LS6.QB_D1, IC1.pin2, IC1.pin16
  N46: 74LS5.QD_D3, 74LS6.QD_D3, IC1.pin4, IC1.pin14
  N47: 74LS5.QF_D5, 74LS6.QF_D5, IC1.pin6, IC1.pin11
  N48: 74LS5.QH_D7, 74LS6.QH_D7, IC1.pin8, IC1.pin9
  GND_3: C11.0, 74LS7.MODE, 74LS7.GND, U3.pin8, 74LS8.GND, C12.0, 74LS9.GND, C13.0, C15.0, IC2.pin12
  VCC_3: C11.1, 74LS7.Vcc, 74LS8.SR_Ds0, 74LS8.SL_Ds7, 74LS8.Vcc, C12.1, 74LS9.SL_Ds7, 74LS9.Vcc, C13.1, C14.+, C15.1, IC2.pin21, IC2.pin24
  N49: 74LS7.Ds_SER, U3.pin7
  N50: 74LS7.D0_A, 74LS7.D1_B, 74LS7.D2_C, 74LS7.D3_D, 74LS8.S0, 74LS8.~CLR, 74LS9.S0, 74LS9.~CLR
  N51: 74LS7.CLK_2, 74LS9.~OE1, 74LS9.~OE2, 74LS9.S1, C14.-
  N52: 74LS7.CLK_1, U3.pin5, 74LS9.CLK
  N53: 74LS7.QD_Q3, U3.pin6, 74LS9.SR_Ds0, IC2.pin23
  N54: 74LS7.QC_Q2, IC2.pin22
  N55: 74LS7.QB_Q1, IC2.pin19
  N56: U3.pin1, 74LS8.~OE1, 74LS8.~OE2, 74LS8.S1
  N57: U3.pin2, 74LS8.CLK
  N58: U3.pin3, IC2.pin20
  N59: U3.pin4, IC2.pin18
  N60: 74LS8.D6_QG, 74LS9.D6_QG, IC2.pin7, IC2.pin10
  N61: 74LS8.D4_QE, 74LS9.D4_QE, IC2.pin5, IC2.pin13
  N62: 74LS8.D2_QC, 74LS9.D2_QC, IC2.pin3, IC2.pin15
  N63: 74LS8.D0_QA, 74LS9.D0_QA, IC2.pin1, IC2.pin17
  N64: 74LS8.QB_D1, 74LS9.QB_D1, IC2.pin2, IC2.pin16
  N65: 74LS8.QD_D3, 74LS9.QD_D3, IC2.pin4, IC2.pin14
  N66: 74LS8.QF_D5, 74LS9.QF_D5, IC2.pin6, IC2.pin11
  N67: 74LS8.QH_D7, 74LS9.QH_D7, IC2.pin8, IC2.pin9
  GND_4: C16.0, 74LS10.MODE, 74LS10.GND, U4.pin8, 74LS11.GND, C17.0, 74LS12.GND, C18.0, C20.0, IC3.pin12
  VCC_4: C16.1, 74LS10.Vcc, 74LS11.SR_Ds0, 74LS11.SL_Ds7, 74LS11.Vcc, C17.1, 74LS12.SL_Ds7, 74LS12.Vcc, C18.1, C19.+, C20.1, IC3.pin21, IC3.pin24
  N68: 74LS10.Ds_SER, U4.pin7
  N69: 74LS10.D0_A, 74LS10.D1_B, 74LS10.D2_C, 74LS10.D3_D, 74LS11.S0, 74LS11.~CLR, 74LS12.S0, 74LS12.~CLR
  N70: 74LS10.CLK_2, 74LS12.~OE1, 74LS12.~OE2, 74LS12.S1, C19.-
  N71: 74LS10.CLK_1, U4.pin5, 74LS12.CLK
  N72: 74LS10.QD_Q3, 74LS12.SR_Ds0, IC3.pin23
  N73: 74LS10.QC_Q2, IC3.pin22
  N74: 74LS10.QB_Q1, IC3.pin19
  N75: U4.pin1, 74LS11.~OE1, 74LS11.~OE2, 74LS11.S1
  N76: U4.pin3, 74LS11.CLK, IC3.pin20
  N77: U4.pin4, IC3.pin18
  N78: U4.pin6, 74LS12.QH'_Q7
  N79: 74LS11.D6_QG, 74LS12.D6_QG, IC3.pin7, IC3.pin10
  N80: 74LS11.D4_QE, 74LS12.D4_QE, IC3.pin5, IC3.pin13
  N81: 74LS11.D2_QC, 74LS12.D2_QC, IC3.pin3, IC3.pin15
  N82: 74LS11.D0_QA, 74LS12.D0_QA, IC3.pin1, IC3.pin17
  N83: 74LS11.QB_D1, 74LS12.QB_D1, IC3.pin2, IC3.pin16
  N84: 74LS11.QD_D3, 74LS12.QD_D3, IC3.pin4, IC3.pin14
  N85: 74LS11.QF_D5, 74LS12.QF_D5, IC3.pin6, IC3.pin11
  N86: 74LS11.QH_D7, 74LS12.QH_D7, IC3.pin8, IC3.pin9
  GND_5: C21.0, 74LS13.MODE, 74LS13.GND, U5.pin8, 74LS14.GND, C22.0, 74LS15.GND, C23.0, C25.0, IC4.pin12
  VCC_5: C21.1, 74LS13.Vcc, U5.pin7, 74LS14.SR_Ds0, 74LS14.SL_Ds7, 74LS14.Vcc, C22.1, 74LS15.SL_Ds7, 74LS15.Vcc, C23.1, C24.+, C25.1, IC4.pin21, IC4.pin24
  N87: 74LS13.D0_A, 74LS13.D1_B, 74LS13.D2_C, 74LS13.D3_D, 74LS14.S0, 74LS14.~CLR, 74LS15.S0, 74LS15.~CLR
  N88: 74LS13.CLK_2, 74LS15.~OE1, 74LS15.~OE2, 74LS15.S1, C24.-
  N89: 74LS13.CLK_1, U5.pin5, 74LS15.CLK
  N90: 74LS13.QD_Q3, 74LS15.SR_Ds0, IC4.pin23
  N91: 74LS13.QC_Q2, IC4.pin22
  N92: 74LS13.QB_Q1, IC4.pin19
  N93: U5.pin1, 74LS14.~OE1, 74LS14.~OE2, 74LS14.S1
  N94: U5.pin3, 74LS14.CLK, IC4.pin20
  N95: U5.pin4, IC4.pin18
  N96: U5.pin6, 74LS14.QH'_Q7
  N97: 74LS14.D6_QG, 74LS15.D6_QG, IC4.pin7, IC4.pin10
  N98: 74LS14.D4_QE, 74LS15.D4_QE, IC4.pin5, IC4.pin13
  N99: 74LS14.D2_QC, 74LS15.D2_QC, IC4.pin3, IC4.pin15
  N100: 74LS14.D0_QA, 74LS15.D0_QA, IC4.pin1, IC4.pin17
  N101: 74LS14.QB_D1, 74LS15.QB_D1, IC4.pin2, IC4.pin16
  N102: 74LS14.QD_D3, 74LS15.QD_D3, IC4.pin4, IC4.pin14
  N103: 74LS14.QF_D5, 74LS15.QF_D5, IC4.pin6, IC4.pin11
  N104: 74LS14.QH_D7, 74LS15.QH_D7, IC4.pin8, IC4.pin9

notes:
  U2
  1   2   3   4   5   6   7   8
  Mk2716 Reader
  7 6 5 4 3 2 1 0 0 1 2
  ------- ADDR -------
  DATA
  8 9         10
  7 6 5 4 3
  --- DATA ---
  --- ADDR ---
  U1
  U4
  U3
  1   3   5   7
  0   2   4   6
  Shift Register Loop Test
  TinyDuino A0 Dsi -- U2 Pin 10 QD
  Address High Test
  2716 replaced by socket connecting addr - data
  TinyDuino A0 Dsi -- U3 Pin 17 QH'
  Address Register Test
  TinyDuino Pin4 Dso -- U4 Pin 11 SR
  Data Register Test

custom parts:
  DIP - 20 pins: 8-Bit Universal Shift/Storage Register
  DIP - 14 pins: 4-Bit Parallel Access Shift Register
  DIP - 24 pins: MK2716T UV-Erasable 2Kx8 EPROM
