# Fritzing sketch TinyDuino Mk2716 Reader (saved by Fritzing 0.9.9b)
breadboards: 1

parts:
  74LS1 = DIP - 20 pins [package="DIP (Dual Inline) [THT]"]
  74LS2 = DIP - 20 pins [package="DIP (Dual Inline) [THT]"]
  74LS3 = DIP - 14 pins [package="DIP (Dual Inline) [THT]"]
  C1 = Ceramic Capacitor [capacitance=100nF voltage=35V package="100 mil [THT, multilayer]"]
  C2 = Ceramic Capacitor [capacitance=100nF voltage=35V package="100 mil [THT, multilayer]"]
  C3 = Ceramic Capacitor [capacitance=100nF voltage=35V package="100 mil [THT, multilayer]"]
  C4 = Electrolytic Capacitor [capacitance=10µF voltage=35V package="100 mil [THT, electrolytic]"]
  S1 = Pushbutton [package="[THT]"]  # not connected
  C5 = Ceramic Capacitor [capacitance=100nF voltage=35V package="100 mil [THT, multilayer]"]
  MK2716T1 = DIP - 24 pins [package="DIP (Dual Inline) [THT]"]
  U1 = mystery part, 8 pins [chip_label="TinyDuino Conn"]

nets:
  N1: 74LS1.S0, 74LS1.~CLR, 74LS2.S0, 74LS2.~CLR, 74LS3.D0_A, 74LS3.D1_B, 74LS3.D2_C, 74LS3.D3_D
  N2: 74LS1.~OE1, 74LS1.~OE2, 74LS1.S1, U1.pin1
  N3: 74LS1.D6_QG, MK2716T1.D1
  N4: 74LS1.D4_QE, MK2716T1.D3
  N5: 74LS1.D2_QC, MK2716T1.D5
  N6: 74LS1.D0_QA, MK2716T1.D7
  GND: 74LS1.GND, 74LS2.GND, 74LS3.MODE, 74LS3.GND, C1.0, C2.0, C3.0, C5.0, MK2716T1.GND, U1.pin8
  VCC: 74LS1.SR_Ds0, 74LS1.SL_Ds7, 74LS1.Vcc, 74LS2.SL_Ds7, 74LS2.Vcc, 74LS3.Vcc, C1.1, C2.1, C3.1, C4.+, C5.1, MK2716T1.Vpp, MK2716T1.VCC
  N7: 74LS1.CLK, U1.pin2
  N8: 74LS1.QB_D1, MK2716T1.D6
  N9: 74LS1.QD_D3, MK2716T1.D4
  N10: 74LS1.QF_D5, MK2716T1.D2
  N11: 74LS1.QH_D7, MK2716T1.D0
  N12: 74LS1.QH'_Q7, U1.pin6
  N13: 74LS2.~OE1, 74LS2.~OE2, 74LS2.S1, 74LS3.CLK_2, C4.-
  N14: 74LS2.D6_QG, MK2716T1.A1
  N15: 74LS2.D4_QE, MK2716T1.A3
  N16: 74LS2.D2_QC, MK2716T1.A5
  N17: 74LS2.D0_QA, MK2716T1.A7
  N18: 74LS2.SR_Ds0, 74LS3.QD_Q3, MK2716T1.A8
  N19: 74LS2.CLK, 74LS3.CLK_1, U1.pin5
  N20: 74LS2.QB_D1, MK2716T1.A6
  N21: 74LS2.QD_D3, MK2716T1.A4
  N22: 74LS2.QF_D5, MK2716T1.A2
  N23: 74LS2.QH_D7, MK2716T1.A0
  N24: 74LS3.Ds_SER, U1.pin7
  N25: 74LS3.QC_Q2, MK2716T1.A9
  N26: 74LS3.QB_Q1, MK2716T1.A10
  N27: MK2716T1.~CE, U1.pin4
  N28: MK2716T1.~OE, U1.pin3

notes:
  U2
  1   2   3   4   5   6   7   8
  Mk2716 Reader
  TinyDuino Pin4
  7 6 5 4 3 2 1 0 0 1 2
  ------- ADDR -------
  DATA
  8 9         10
  7 6 5 4 3
  --- DATA ---
  --- ADDR ---
  U1
  U4
  U3
  1   3   5   7
  0   2   4   6

custom parts:
  DIP - 20 pins: 8-Bit Universal Shift/Storage Register
  DIP - 14 pins: 4-Bit Parallel Access Shift Register
  DIP - 24 pins: MK2716T UV-Erasable 2Kx8 EPROM
