# Fritzing sketch z80 reset test (saved by Fritzing 0.9.9b)
breadboards: 1

parts:
  U1 = 555 Timer [package="DIP8 [THT]"]
  U2 = 555 Timer [package="DIP8 [THT]"]
  C1 = Ceramic Capacitor [capacitance=0.01mF voltage=35V package="100 mil [THT, multilayer]"]
  R1 = Resistor [tolerance=±5% resistance=1k package=THT]
  R2 = Resistor [tolerance=±10% resistance=75.1k package=THT]
  C3 = Ceramic Capacitor [capacitance=10nF voltage=35V package="100 mil [THT, multilayer]"]
  C4 = Ceramic Capacitor [capacitance=0.1µF voltage=35V package="100 mil [THT, multilayer]"]
  C5 = Ceramic Capacitor [capacitance=0.01µF voltage=35V package="100 mil [THT, multilayer]"]
  C6 = Electrolytic Capacitor [capacitance=0.33µF voltage=35V package="100 mil [THT, electrolytic]"]
  R6 = Resistor [tolerance=±5% resistance=4.7k package=THT]
  Q1 = NPN-Transistor [part_number=2N3904 package="TO92 [THT]"]
  R7 = Resistor [tolerance=±5% resistance=4.7k package=THT]
  R8 = Resistor [tolerance=±5% resistance=2.2k package=THT]
  C7 = Electrolytic Capacitor [capacitance=0.33µF voltage=35V package="100 mil [THT, electrolytic]"]

nets:
  N1: U1.Ground, U2.Ground, C1.1, C3.0, C4.0, C5.0, C6.-, Q1.E, C7.-
  N2: U1.Trigger, U1.Threshold, R2.Pin_0, C4.1
  N3: U1.Output, R6.Pin_0
  N4: U1.Reset, U1.Vcc_Supply_Voltage, U2.Reset, U2.Vcc_Supply_Voltage, R1.Pin_1, C3.1, R7.Pin_0, C7.+
  N5: U1.Control_Voltage, C1.0
  N6: U1.Discharge, R1.Pin_0, R2.Pin_1
  N7: U2.Trigger, U2.Threshold, C6.+, R6.Pin_1
  N8: U2.Output, R8.Pin_0
  N9: U2.Control_Voltage, C5.1
  N10: Q1.B, R8.Pin_1
  N11: Q1.C, R7.Pin_1

notes:
  Z80 Reset
  Schmitt Trigger
  Square Wave Gen
  .01uF
  .1uF
  .33uF
  +++
  Delay RC
  10uF
